# Fritzing sketch arduino-breadboard (saved by Fritzing 0.9.0b)
breadboards: 1

parts:
  Arduino_Uno = Arduino Uno (Rev3)
  MAX232 = RS232 Transceiver [package=dil16]
  C232_3 = Electrolytic Capacitor [capacitance=10µF package="100 mil [THT, electrolytic]"]
  C232_1 = Electrolytic Capacitor [capacitance=10µF package="100 mil [THT, electrolytic]"]
  C232_2 = Electrolytic Capacitor [capacitance=10µF package="100 mil [THT, electrolytic]"]
  C232_4 = Electrolytic Capacitor [capacitance=10µF package="100 mil [THT, electrolytic]"]
  D-SUB = DB9 Connector [package=db9]
  V1 = DC Power [voltage=30V]

nets (from the schematic view):
  N1: Arduino_Uno.D8, MAX232.T2IN
  N2: Arduino_Uno.D9_PWM, MAX232.R2OUT
  5V: Arduino_Uno.5V, MAX232.VCC, C232_2.-
  N3: Arduino_Uno.GND, V1.V-
  N4: MAX232.C1+, C232_1.-
  N5: MAX232.V+, C232_2.+
  N6: MAX232.C1-, C232_1.+
  N7: MAX232.C2+, C232_3.-
  N8: MAX232.C2-, C232_3.+
  N9: MAX232.V-, C232_4.-
  N10: MAX232.T2OUT, D-SUB.3
  N11: MAX232.R2IN, D-SUB.2
  N12: MAX232.GND, C232_4.+, D-SUB.5

notes:
  oven rs232
